# Fritzing sketch WardIONano (saved by Fritzing 0.8.7b)
breadboards: 2

parts:
  M1 = MAX30102
  Componente1 = Arduino Nano (Rev3.0)
  Componente2 = OLED Monochrome 128x64 1.3 inch [part_number=938]
  U1 = ESP32-38PinWide [part_number=ESP32-38PinWide]
  DS1 = DS18B20 1-Wire Temperature Sensor Probe Cable
  R1 = Resistor [tolerance=±5% resistance=4.7k package=THT]
  S1 = Pushbutton [package=THT]
  S2 = Pushbutton [package=THT]
  S3 = Pushbutton [package=THT]

nets:
  VIN: M1.VIN, Componente1.3V3
  N1: M1.SCL, Componente1.A5
  N2: M1.SDA, Componente1.A4
  GND: M1.GND, Componente1.GND, Componente2.GND, U1.GND, DS1.GND, S1.leg1, S2.leg1, S3.leg1
  N3: Componente1.D10, U1.GPIO16
  N4: Componente1.D11/MOSI, U1.GPIO17
  VIN_2: Componente1.VIN, U1.VIN
  N5: Componente2.MOSI_SDA, U1.GPIO21
  N6: Componente2.DC_SA0, U1.GPIO22
  VIN_3: Componente2.VIN, U1.3.3, DS1.VDD, R1.Pin_1
  N7: U1.GPIO25, S1.leg0
  N8: U1.GPIO26, S3.leg0
  N9: U1.GPIO27, S2.leg0
  N10: U1.GPIO19, DS1.shield, R1.Pin_0

custom parts:
  MAX30102: Oximeter module using the MAX30102 chip. You may wish to read (and check your module) this post on power problems with these modules: https://reedpaper.wordpress.com/2018/08/22/pulse-oximeter-max30100-max30102-how-to-fix-wrong-board/ . As usual, if you want the mounting holes in pcb, you need to drag a hole over the pad in silkscreen to actually drill the hole (by default they are not drilled)
  OLED Monochrome 128x64 1.3 inch: These displays are small, only about 1.3" diagonal, but very readable due to the high contrast of an OLED display. This display is made of 128x64 individual white OLED pixels, each one is turned on or off by the controller chip. Because the display makes its own light, no backlight is required. This reduces the power required to run the OLED and is why the display has such high contrast; we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
  ESP32-38PinWide: Generic 38-Pin ESP32 with wide format (only access to one side of pins on a breadboard) based on Stephen Lilley's HiLetgo ESP-WROOM-32 ESP32 ESP-32S Development Board.
